// Digital circuit state_machine_digital.dig as structural Verilog
module state_machine_digital (
  input  photocell2,
  input  photocell3,
  input  photocell4,
  input  clk,
  input  photocell1,
  input  in_18,
  output out_3,
  output out_4,
  output out_5,
  output out_6,
  output out_7,
  output out_9,
  output [7:0] out_10,
  output [7:0] out_11,
  output out_12,
  output [7:0] out_14,
  output [7:0] out_15,
  output out_16
);

  wire u_tof_mimic_tof1, u_tof_mimic_tof2, u_tof_mimic_tof3, u_tof_mimic_tof4;
  wire [7:0] u_RegistroIncDec8bit_2_q, u_RegistroIncDec8bit_q;

  tof_mimic #(.applicationType("GHDL"), .Code_File("C:\\Users\\davol\\embedded_system_design\\digital\\src\\tof_sensors_mimic.vhd")) u_tof_mimic (
    .i1(photocell1), .i2(photocell2), .i3(photocell3), .i4(photocell4), .mv_msg(u_RegistroIncDec8bit_q),
    .tof1(u_tof_mimic_tof1), .tof2(u_tof_mimic_tof2), .tof3(u_tof_mimic_tof3), .tof4(u_tof_mimic_tof4));
  decoder_5_6 #(.applicationType("GHDL"), .Code_File("C:\\Users\\davol\\embedded_system_design\\digital\\src\\decoder.vhd")) u_decoder_5_6 (
    .i1(u_tof_mimic_tof1), .i2(u_tof_mimic_tof2), .i3(u_tof_mimic_tof3), .i4(u_tof_mimic_tof4), .ck(clk),
    .msg(u_RegistroIncDec8bit_q), .o1(out_3), .o2(out_4), .o3(out_5), .o4(out_6), .mv(out_7), .pr(out_9),
    .picked(out_10[5]), .err(out_10[6]));
  RegistroIncDec8bit #(.applicationType("GHDL")) u_RegistroIncDec8bit (
    .D(out_14), .Set(out_16), .Inc(1'b0), .Dec(1'b0), .Clk(clk), .Reset(1'b0), .Q(u_RegistroIncDec8bit_q));
  write_uart_sm #(.applicationType("GHDL"), .Code_File("C:\\Users\\davol\\embedded_system_design\\digital\\src\\write_uart_state_machine.vhd")) u_write_uart_sm (
    .state_vector({out_9, out_10[6:5], out_7, out_6, out_5, out_4, out_3}), .ext_error(out_10[6]), .clk(clk),
    .data_write(out_11), .data_write_bool(out_12));
  RegistroIncDec8bit #(.applicationType("GHDL")) u_RegistroIncDec8bit_2 (
    .D({8{1'b0}}), .Set(in_18), .Inc(in_18), .Dec(1'b0), .Clk(clk), .Reset(1'b0), .Q(u_RegistroIncDec8bit_2_q));
  // ComPort #(.comPort("COM6")) COM6: pin names not known; wires that end beside it: out_11, out_12, 1'b1, clk, out_14, out_16
  Seven_Seg_Hex seven_seg_hex_1 (.d(u_RegistroIncDec8bit_2_q[3:0]), .dp(1'b0));
  Seven_Seg_Hex seven_seg_hex_2 (.d(u_RegistroIncDec8bit_2_q[7:4]), .dp(1'b0));

  assign {out_10[7], out_10[4:0]} = {out_9, out_7, out_6, out_5, out_4, out_3};
  assign out_15 = out_11;
endmodule

/* Code of tof_mimic:
library ieee;
use ieee.std_logic_1164.all;

entity tof_mimic is
	port ( i1, i2, i3, i4: in std_logic;
           mv_msg: in std_logic_vector(7 downto 0);
	       tof1, tof2, tof3, tof4: out std_logic);
end entity tof_mimic;

architecture arc_tof_mimic of tof_mimic is
    signal mv_counter: std_logic := '0';
    signal state_msg: std_logic_vector(7 downto 0) := "00000000";
begin
    comb: process(mv_counter, i1, i2, i3, i4)
    begin
        tof1 <= i1;
        tof2 <= i2;
        tof3 <= i3;
        tof4 <= i4;
        if (mv_counter = '1') then
            tof1 <= '0';
            tof2 <= '0';
            tof3 <= '0';
            tof4 <= '0';
        end if;
    end process;
    
    upd_msg: process(mv_msg)
    begin
        if mv_msg /= "ZZZZZZZZ" then
            state_msg <= mv_msg;
        end if;
    end process;

    upd: process(state_msg, i1, i2, i3, i4)
    begin
        if (i1'event and i1 = '1') then
            mv_counter <= '0';
        elsif (i2'event and i2 = '1') then
            mv_counter <= '0';
        elsif (i3'event and i3 = '1') then
            mv_counter <= '0';
        elsif (i4'event and i4 = '1') then
            mv_counter <= '0';
        elsif (state_msg'event) then
            if state_msg = "00010000" then
                mv_counter <= '1';
            else    
                mv_counter <= '0';
            end if;
        end if;
    end process;
end arc_tof_mimic;
*/

/* Code of decoder_5_6:
library ieee;
use ieee.std_logic_1164.all;

entity decoder_5_6 is
	port ( i1, i2, i3, i4, ck: in std_logic;
           msg: in std_logic_vector(7 downto 0);
	       o1, o2, o3, o4, mv, pr, picked, err: out std_logic);
end entity decoder_5_6;

architecture arc_decoder_5_6 of decoder_5_6 is
    signal pr_state: std_logic:='0';
    signal mv_state: std_logic:='0';
    signal idle_state: std_logic:='0';
    signal combined_state: std_logic_vector(2 downto 0) := "000";
    signal previous_i4: std_logic;
begin
    process(combined_state, i1, i2, i3, i4) is
        variable combined_input: std_logic_vector(3 downto 0);
    begin
        o1 <= '0';
        o2 <= '0';
        o3 <= '0';
        o4 <= '0';
        pr <= combined_state(0);
        mv <= combined_state(2);
        picked <= '0';
        err <= '0';
        combined_input := i4 & i3 & i2 & i1;
        if combined_state(2) then -- Con
            mv <= '0';
            case combined_input is
                when "0001" =>
                    o1 <= '1';
                when "0010" =>
                    o2 <= '1';
                when "0100" =>
                    o3 <= '1';
                when "1000" =>
                    o4 <= '1';
                when "0000" =>
                    mv <= '1';
                when others =>
                    err <= '1';
            end case;
        elsif combined_state(0) = '1' and i4 = '0' and previous_i4 = '1' then -- Picked condition
            picked <= '1';
        elsif combined_state(1) or combined_state(2) then -- Idle should be interrupted when vial at first station
            if (combined_input = "0001") then
                o1 <= '1';
                pr <= '0';
            end if;
        end if;
    end process;

    process(msg) is  
    begin
        combined_state <= "000";
        if (msg = "10000000") then -- Process
            combined_state <= "001";
        elsif (msg = "00000000" or msg = "00001001") then -- Idle
            combined_state <= "010";
        elsif (msg = "00010000") then -- Move
            combined_state <= "100";
        end if;
    end process;

    process(ck) is
    begin
        if (ck'event and ck = '1') then
            previous_i4 <= i4;
        end if;
    end process;


end arc_decoder_5_6;
*/

/* Code of RegistroIncDec8bit:
library ieee;
use ieee.std_logic_1164.all;
use ieee.numeric_std.all;
-- per dare un senso agli operatori +1 e -1:
use ieee.std_logic_unsigned.all; 


entity RegistroIncDec8bit is

	port 
	(
		Q : out  std_logic_vector(7 downto 0);
		D : in  std_logic_vector(7 downto 0);
		Set: in std_logic;
		Inc: in std_logic;
		Dec: in std_logic;
		Clk : in std_logic;
		Reset : in std_logic
	);

end RegistroIncDec8bit;
architecture behav of RegistroIncDec8bit is
signal currVal  :  std_logic_vector(7 downto 0);
signal nextVal :  std_logic_vector(7 downto 0);
signal IncDecSet :  std_logic_vector(2 downto 0); -- segnale ausiliario
begin

	process(clk)
	begin
		if (clk='1' and clk'event) then
			if (reset ='1') then	
				currVal <= (others =>'0');
			else
				currVal <= nextVal;
			end if;
		end if;
	end process;
	
	-- selezione del prossimo valore interno
	IncDecSet <= Inc & Dec & Set;
	with IncDecSet select
		nextVal <= D		when "001",
			   currVal + 1  when "100",
			   currVal - 1  when "010",
			   currVal		when others;  -- others assures combinatorial synthesis	
			   				  
	Q <= currVal;

end behav;
*/

/* Code of write_uart_sm:
library ieee;
use ieee.std_logic_1164.all;

entity write_uart_sm is
	port ( state_vector: in std_logic_vector(7 downto 0);
           ext_error: in std_logic;
           clk: in std_logic;
	       data_write: out std_logic_vector(7 downto 0); 
           data_write_bool: out std_logic);
end entity write_uart_sm;

architecture arc_write_uart_sm of write_uart_sm is
    signal state_changed: std_logic;
    signal current_state: std_logic_vector(7 downto 0);
begin
    process(clk) is
    begin
        if (clk = '1' and clk'event) then
            data_write <= state_vector;
            if (state_vector /= current_state and ext_error = '0') then
                state_changed <= '1';
                current_state <= state_vector;
                data_write_bool <= '1';
            else
                data_write_bool <= '0';
            end if;
        end if;
    end process;
end arc_write_uart_sm;
*/
